# Fritzing sketch alarm-machine (saved by Fritzing 0.9.3b)
circuit board: 8cm x 5.64cm
breadboards: 1

parts:
  Part1 = Arduino Uno (Rev3)
  IC1 = IC, DIP package, 28 pins [chip_label=TWE-LITE]
  IC2 = IC, SIP package, 4 pins [chip_label=RTC]
  IC3 = IC, SIP package, 5 pins [chip_label=LCD]
  R1 = Resistor [tolerance=±5% resistance=10k package=THT]
  R2 = Resistor [tolerance=±5% resistance=10k package=THT]
  R3 = Resistor [tolerance=±5% resistance=10k package=THT]
  S4 = Pushbutton [package="[THT]"]
  LED1 = LED - 5mm [color="Green (570nm)" package="5 mm [THT]"]
  R4 = Resistor [tolerance=±5% resistance=10k package=THT]
  IC4 = IC, SIP package, 3 pins [chip_label="Melody IC"]
  J1 = Piezo Speaker
  S1 = Pushbutton [package=THT]
  S2 = Pushbutton [package=THT]
  S3 = Pushbutton [package=THT]
  R5 = Resistor [tolerance=±5% resistance=100 package=THT]
  R6 = Trimmer Potentiometer [maximum_resistance=10kΩ package=THT]

nets:
  N1: Part1.A0, IC1.pin11
  N2: Part1.A1, R6.wiper
  N3: Part1.A4/SDA, IC2.pin3, IC3.pin4
  N4: Part1.A5/SCL, IC2.pin4, IC3.pin3
  N5: Part1.D8, R1.Pin_1, S1.leg0
  N6: Part1.D9_PWM, R2.Pin_1, S2.leg0
  N7: Part1.D10_PWM/SS, R3.Pin_1, S3.leg0
  N8: Part1.D11_PWM/MOSI, IC4.pin2
  GND: Part1.GND, IC1.pin13, IC1.pin14, IC1.pin22, IC1.pin23, IC1.pin24, IC1.pin25, IC2.pin1, IC3.pin5, S4.Pin_1, S4.Pin_2, LED1.cathode, IC4.pin1, J1.pin1, S1.leg1, S2.leg1, S3.leg1, R6.leg1
  N9: Part1.D6_PWM, R5.Pin_0
  N10: Part1.D7, S4.Pin_4, R4.Pin_1
  3.3V: Part1.3V3, IC1.pin28, IC2.pin2, IC3.pin1, IC3.pin2, R1.Pin_0, R2.Pin_0, R3.Pin_0, R4.Pin_0, R6.leg2
  N11: LED1.anode, R5.Pin_1
  N12: IC4.pin3, J1.pin2
