# Fritzing sketch sensor (saved by Fritzing 0.9.3b)
circuit board: 7.2cm x 4.75cm
breadboards: 1

parts:
  BAT1 = Battery Holders [package=battery-aa-kit]
  IC1 = IC, DIP package, 6 pins [chip_label=IC]
  R1 = Photocell (LDR) [package=THT]
  IC2 = IC, DIP package, 28 pins [chip_label=TWE-LITE]
  S1 = Toggle Switch [package=THT]
  R2 = Resistor [tolerance=±5% resistance=470 package=THT]
  R3 = Resistor [tolerance=±5% resistance=10k package=THT]
  R4 = Resistor [tolerance=±5% resistance=10k package=THT]

nets:
  N1: BAT1.+, S1.COM
  GND: BAT1.-, IC1.pin6, IC2.pin14, IC2.pin22, IC2.pin23, IC2.pin24, IC2.pin27, R2.Pin_1
  3.3V: IC1.pin2, IC2.pin28, R3.Pin_0
  N2: IC1.pin3, IC1.pin4, S1.L2
  N3: R1.pin_0, IC2.pin25, R3.Pin_1, R4.Pin_0
  N4: R1.pin_1, R2.Pin_0, R4.Pin_1
